# Fritzing sketch WiringDiagram_Pixhawk (saved by Fritzing 0.9.9b)

parts:
  Teensy_3_2 = Teensy 3.1
  Part2 = I2C level shifter bidirectional
  RE3 = Rotary Encoder [package=THT]
  RE4 = Rotary Encoder [package=THT]
  U5 = mystery part, 4 pins [chip_label=TODO]

nets:
  GND: Teensy_3_2.GND, Part2.GND, RE3.EncoderPinB, RE4.EncoderPinB, U5.pin4
  N1: Teensy_3_2.D3, Part2.LV2
  N2: Teensy_3_2.D4, Part2.LV1
  N3: Teensy_3_2.A4/D18, U5.pin3
  N4: Teensy_3_2.A5/D19, U5.pin2
  N5: Teensy_3_2.3V3, Part2.LV
  N6: Teensy_3_2.Vin, U5.pin1
  N7: Part2.HV1, RE4.EncoderPinC
  N8: Part2.HV2, RE3.EncoderPinC
  N9: Part2.HV, RE3.EncoderPinA, RE4.EncoderPinA
