# Fritzing sketch WiringDiagram (saved by Fritzing 0.9.9b)

parts:
  Teensy_3_1 = Teensy 3.1
  RE1 = Rotary Encoder [package=THT]
  RE2 = Rotary Encoder [package=THT]
  Part1 = I2C level shifter bidirectional
  U1 = Hirose DF13 Series Header [part_number=DF13A-4P-1.25H package=DF13A-4P-1.25H]
  U2 = Hirose DF13 Series Header [part_number=DF13A-4P-1.25H package=DF13A-4P-1.25H]
  R1 = Resistor [tolerance=±5% power=0.25 resistance=4.7k package=THT]
  R2 = Resistor [tolerance=±5% power=0.25 resistance=4.7k package=THT]

nets:
  GND: Teensy_3_1.GND, RE1.EncoderPinB, RE2.EncoderPinB, Part1.GND, U1.4, U2.4
  N1: Teensy_3_1.D3, Part1.LV4
  N2: Teensy_3_1.D4, Part1.LV3
  N3: Teensy_3_1.A4/D18, U1.3
  N4: Teensy_3_1.A5/D19, U1.2
  N5: Teensy_3_1.A8/D22, Part1.LV1, R1.Pin_1
  N6: Teensy_3_1.A9/D23, Part1.LV2, R2.Pin_1
  N7: Teensy_3_1.3V3, Part1.LV, R1.Pin_0, R2.Pin_0
  N8: Teensy_3_1.Vin, RE1.EncoderPinA, RE2.EncoderPinA, Part1.HV, U1.1, U2.1
  N9: RE1.EncoderPinC, Part1.HV4
  N10: RE2.EncoderPinC, Part1.HV3
  N11: Part1.HV1, U2.2
  N12: Part1.HV2, U2.3
